# Fritzing sketch uzinagaz_sketch (saved by Fritzing 0.8.0b)
breadboards: 1

parts:
  Composants1 = Arduino Uno (Rev3)
  RHT1 = Humidity and Temperature Sensor RHT03
  part = Resistor [tolerance=±10% resistance=10k package=THT]
  part_2 = Resistor [tolerance=±5% resistance=10k package=THT]
  part_3 = Resistor [tolerance=±5% resistance=10k package=THT]
  MQ_Gas_Sensor_Carrier1 = Pololu MQ Gas Sensor Carrier [part_number=1479 package=PCB]
  MQ_Gas_Sensor_Carrier2 = Pololu MQ Gas Sensor Carrier [part_number=1479 package=PCB]

nets:
  N1: Composants1.A0, part_3.Pin_1, MQ_Gas_Sensor_Carrier1.OUT
  N2: Composants1.A1, part_2.Pin_1, MQ_Gas_Sensor_Carrier2.OUT
  GND: Composants1.GND, RHT1.GND_2, part_2.Pin_0, part_3.Pin_0, MQ_Gas_Sensor_Carrier1.GND, MQ_Gas_Sensor_Carrier2.GND
  N3: Composants1.D12/MISO, RHT1.Data-signal, part.Pin_1
  VCC: Composants1.5V, RHT1.Vcc, part.Pin_0, MQ_Gas_Sensor_Carrier1.VCC, MQ_Gas_Sensor_Carrier2.VCC

custom parts:
  Pololu MQ Gas Sensor Carrier: Pololu Item #1479 This carrier board is designed to work with any of the MQ-series gas sensors, simplifying the interface from 6 to 3 pins—ground, power and analog voltage output—that are broken out with a 0.1" spacing, making the board compatible with 0.1" headers and standard breadboards and perfboards. This board has two mounting holes and provides convenient pads for mounting the gas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
